# Fritzing sketch basic (saved by Fritzing 0.8.7b)
breadboards: 1

parts:
  Part1 = Arduino Uno (Rev3)
  R1 = Resistor [tolerance=±5% resistance=8.8 package=THT]
  HDMI_0 = Header 4 [package=jst-4-pth]
  HDMI_1 = Header 4 [package=jst-4-pth]
  S1 = SWITCH-MOMENTARY-2 [package=tactile-pth]
  S2 = SWITCH-MOMENTARY-2 [package=tactile-pth]
  S3 = SWITCH-MOMENTARY-2 [package=tactile-pth]
  S4 = SWITCH-MOMENTARY-2 [package=tactile-pth]
  S5 = SWITCH-MOMENTARY-2 [package=tactile-pth]
  R2 = Resistor [tolerance=±5% resistance=8.8 package=THT]
  R3 = Resistor [tolerance=±5% resistance=2.2k package=THT]
  R4 = Resistor [tolerance=±5% resistance=2.2k package=THT]
  R5 = Resistor [tolerance=±5% resistance=2.2k package=THT]
  R6 = Resistor [tolerance=±5% resistance=2.2k package=THT]

nets:
  N1: Part1.D8, HDMI_0.3, R4.Pin_0
  N2: Part1.D9_PWM, HDMI_1.2, R5.Pin_0
  N3: Part1.D10_PWM/SS, HDMI_1.3, R6.Pin_0
  GND: Part1.GND, HDMI_0.4, HDMI_1.4, S1.2, S2.2, S3.2, S4.2, S5.2
  N4: Part1.D2, S1.1
  N5: Part1.D3_PWM, S2.1
  N6: Part1.D4, S3.1
  N7: Part1.D5_PWM, S4.1
  N8: Part1.D6_PWM, S5.1
  N9: Part1.D7, HDMI_0.2, R3.Pin_0
  5V: Part1.5V, R1.Pin_0, R2.Pin_0, R3.Pin_1, R4.Pin_1, R5.Pin_1, R6.Pin_1
  N10: R1.Pin_1, HDMI_0.1
  N11: HDMI_1.1, R2.Pin_1
